# Fritzing sketch GasSensor (saved by Fritzing 0.9.3b)

parts:
  U1 = NodeMCU V3.0
  Part1 = BME280 Breakout
  J1 = female pin header, 4 pins [form="♀ (female)"]

nets:
  N1: U1.D1, Part1.SCK/SCL, J1.pin1
  N2: U1.D2, Part1.SDI/SDA, J1.pin2
  3V3: U1.3V3, Part1.3.3V, J1.pin3
  GND: U1.GND, Part1.GND, J1.pin4

notes:
  Grove multigas sensor to NodeMCU
  Yellow - SCL - D1
  White - SDA - D2
  Red - VCC - 3V
  Black - GND - GND
  SCL
  SDA
  VCC
  GND
  Grove Multiigas Sensor

custom parts:
  NodeMCU V3.0: ESP8266 based NodeMCU
